# Fritzing sketch Light Sensor Schematic (saved by Fritzing 0.9.3b)
breadboards: 1

parts:
  Part1 = Arduino Uno (Rev3)
  R1 = Photocell (LDR) [package=THT]
  R2 = Photocell (LDR) [package=THT]
  R3 = Resistor [tolerance=±5% resistance=10k package="0402 [SMD]"]
  R4 = Resistor [tolerance=±5% resistance=10k package="0402 [SMD]"]

nets:
  N1: Part1.A0, R2.pin_1, R3.Pin_1
  N2: Part1.A1, R1.pin_1, R4.Pin_1
  N3: Part1.5V, R1.pin_0, R2.pin_0
  N4: Part1.GND, R3.Pin_0, R4.Pin_0
