# Fritzing sketch Moisture Sensor Schematic (saved by Fritzing 0.9.2b)
breadboards: 1

parts:
  Part1 = Arduino Uno (Rev3)
  PART1 = SparkFun Soil Moisture Sensor [part_number=SEN-13322]  # not connected
  J1 = screw terminal, 3 pins

nets:
  N1: Part1.A0, J1.pin1
  N2: Part1.5V, J1.pin3
  N3: Part1.GND, J1.pin2

custom parts:
  SparkFun Soil Moisture Sensor: The SparkFun Soil Moisture Sensor is a simple breakout for measuring the moisture in soil and similar materials.
